# Fritzing sketch GPS_1_44_TFT (saved by Fritzing 0.9.3b)

parts:
  WeMos_D1_Mini1 = WeMos D1 Mini
  U2 = NEO 6M GPS
  U1 = 2.4" TFT LCD screen, SPI, Touch-enabled
  U3 = NEO 6M GPS
  U4 = 2.4" TFT LCD screen, SPI, Touch-enabled
  WeMos_D1_Mini2 = WeMos D1 Mini

nets:
  N1: WeMos_D1_Mini1.D0, U1.CS
  N2: WeMos_D1_Mini1.D1, U2.VCC
  N3: WeMos_D1_Mini1.D2, U2.GND
  N4: WeMos_D1_Mini1.D5, U1.SCL
  N5: WeMos_D1_Mini1.D6, U1.DC
  N6: WeMos_D1_Mini1.D7, U1.SDA
  N7: U1.LED, U1.RESET, U1.VCC
  N8: U3.GND, WeMos_D1_Mini2.D4
  N9: U3.VCC, WeMos_D1_Mini2.D1
  N10: U4.LED, U4.RESET, U4.VCC
  N11: U4.SCL, WeMos_D1_Mini2.D5
  N12: U4.SDA, WeMos_D1_Mini2.D7
  N13: U4.DC, WeMos_D1_Mini2.D2
  N14: U4.CS, WeMos_D1_Mini2.D0

notes:
  //UTFT myGLCD ( ST7735, D7, D5, D8, D2, D2 );
  UTFT myGLCD ( ST7735, D7, D5, D0, D6, D6 );

custom parts:
  NEO 6M GPS: uSD module
  2.4" TFT LCD screen, SPI, Touch-enabled: 2.4", ILI9341-based TFT LCD screen with touch-sensing using the XPT2046 controller, SPI-compatible. There is also an SD-card version that is non-touch enabled but uses exactly the same board and pinout. This part is for both, though it should be noted that the SD reader and the touch screen are mutually incompatible
