# Fritzing sketch GPS_2_4_TFT_Touch (saved by Fritzing 0.9.3b)

parts:
  U1 = 2.4" TFT LCD screen, SPI, Touch-enabled
  WeMos_D1_Mini1 = WeMos D1 Mini
  U2 = NEO 6M GPS

nets:
  N1: U1.T_IRQ, WeMos_D1_Mini1.D3
  N2: U1.T_DO, WeMos_D1_Mini1.D6
  N3: U1.T_DIN, U1.SDA, WeMos_D1_Mini1.D7
  N4: U1.T_CS, WeMos_D1_Mini1.D0
  N5: U1.T_CLK, U1.SCL, WeMos_D1_Mini1.D5
  N6: U1.LED, U1.RESET, WeMos_D1_Mini1.3V3
  N7: U1.DC, WeMos_D1_Mini1.D2
  N8: U1.CS, WeMos_D1_Mini1.D8
  N9: WeMos_D1_Mini1.D1, U2.VCC
  N10: WeMos_D1_Mini1.D4, U2.GND

custom parts:
  2.4" TFT LCD screen, SPI, Touch-enabled: 2.4", ILI9341-based TFT LCD screen with touch-sensing using the XPT2046 controller, SPI-compatible. There is also an SD-card version that is non-touch enabled but uses exactly the same board and pinout. This part is for both, though it should be noted that the SD reader and the touch screen are mutually incompatible
  NEO 6M GPS: uSD module
