# Fritzing sketch Untitled Sketch 2 (saved by Fritzing 0.9.3b)
circuit board: 10cm x 10cm

parts:
  WeMos_D1_Mini1 = WeMos D1 Mini
  Part1 = BME280 Breakout
  Grove1 = Grove OLED 128x96
  WeMos_D1_Mini_Relay_Shield_V1 = WeMos D1 Mini Relay Shield V2

nets:
  3V3: WeMos_D1_Mini1.3V3, Grove1.VCC, WeMos_D1_Mini_Relay_Shield_V1.3V3
  N1: WeMos_D1_Mini1.D1, Part1.SCK/SCL, Grove1.SCL
  N2: WeMos_D1_Mini1.D2, Part1.SDI/SDA, Grove1.SDA
  N3: WeMos_D1_Mini1.D4, WeMos_D1_Mini_Relay_Shield_V1.D4
  N4: WeMos_D1_Mini1.G, Grove1.GND
