# Fritzing sketch Untitled Sketch (saved by Fritzing 0.9.3b)

parts:
  WeMos_D1_Mini1 = WeMos D1 Mini
  R1 = Resistor [tolerance=±5% resistance=220 package=THT]
  LED1 = LED - 5mm [color="Blue (505nm)" package="5 mm [THT]"]
  LED2 = LED - 5mm [color="Green (570nm)" package="5 mm [THT]"]
  R2 = Resistor [tolerance=±5% resistance=220 package=THT]
  Часть1 = Adafruit_BMP280
  DS1 = DS18B20 1-Wire Temperature Sensor [part_number=DS18B20]
  J1 = Basic Servo
  R3 = Resistor [tolerance=±5% resistance=4.7k package=THT]

nets:
  3V3: WeMos_D1_Mini1.3V3, DS1.VDD, R3.Pin_1
  5V: WeMos_D1_Mini1.5V, J1.vcc
  N1: WeMos_D1_Mini1.D0, LED1.anode
  N2: WeMos_D1_Mini1.D1, Часть1.SCK/SCL
  N3: WeMos_D1_Mini1.D2, Часть1.SDI/SDA
  N4: WeMos_D1_Mini1.D3, J1.pulse
  N5: WeMos_D1_Mini1.D4, DS1.DQ, R3.Pin_0
  N6: WeMos_D1_Mini1.D5, LED2.anode
  GND: WeMos_D1_Mini1.G, R1.Pin_0, R2.Pin_0, Часть1.GND, DS1.GND
  N7: R1.Pin_1, LED1.cathode
  N8: LED2.cathode, R2.Pin_1
  N9: Часть1.VIN, Часть1.CS

custom parts:
  Adafruit_BMP280: Bosch has stepped up their game with their new BMP280 sensor, an environmental sensor with temperature, barometric pressure that is the next generation upgrade to the BMP085/BMP180/BMP183. This sensor is great for all sorts of weather sensing and can even be used in both I2C and SPI! This precision sensor from Bosch is the best low-cost, precision sensing solution for measuring barometric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
